// Logisim project Zad_3.circ as structural Verilog: 9 circuits, main circuit SR_Latch
module SR_Latch (
  input  R,
  input  S,
  output Q,
  output Q0
);

  nor nor_1 (Q, R, Q0);
  nor nor_2 (Q0, Q, S);
endmodule

module D_Latch (
  input  CLK,
  input  D,
  output Q,
  output Q0
);

  wire and_1_out, and_2_out, not_1_out;

  and and_1 (and_1_out, CLK, not_1_out);
  not not_1 (not_1_out, D);
  and and_2 (and_2_out, CLK, D);
  SR_Latch sr_latch_1 (.Q(Q), .Q0(Q0), .S(and_2_out), .R(and_1_out));
endmodule

module D_Flip_Flop (
  input  CLK,
  input  D,
  output Q
);

  wire d_latch_1_q, not_1_out;

  not not_1 (not_1_out, CLK);
  D_Latch d_latch_1 (.Q(d_latch_1_q), .D(D), .CLK(not_1_out));  // open: Q0
  D_Latch d_latch_2 (.Q(Q), .D(d_latch_1_q), .CLK(CLK));  // open: Q0
endmodule

module Enabled_Flip_Flop (
  input  CLK,
  input  EN,
  input  D,
  output Q
);

  wire and_1_out;

  and and_1 (and_1_out, CLK, EN);
  D_Flip_Flop d_flip_flop_1 (.Q(Q), .CLK(and_1_out), .D(D));
endmodule

module Resettable_Flip_Flop (
  input  CLK,
  input  D,
  input  RESET,
  output Q
);

  wire and_1_out, not_1_out;

  not not_1 (not_1_out, RESET);
  and and_1 (and_1_out, D, not_1_out);
  D_Flip_Flop d_flip_flop_1 (.Q(Q), .CLK(CLK), .D(and_1_out));
endmodule

module async_reset_D_Latch (
  input  CLK,
  input  Reset,
  input  D,
  output out_4,
  output out_5
);

  wire and_1_out, and_2_out, not_1_out, not_2_out, not_3_out, or_1_out;

  not not_1 (not_1_out, CLK);
  or or_1 (or_1_out, not_1_out, Reset);
  not not_2 (not_2_out, or_1_out);
  and and_1 (and_1_out, not_2_out, not_3_out);
  not not_3 (not_3_out, D);
  and and_2 (and_2_out, not_2_out, D);
  SR_Latch sr_latch_1 (.Q(out_4), .Q0(out_5), .S(and_2_out), .R(and_1_out));
endmodule

module Async_reset_Flip_Flop (
  input  CLK,
  input  D,
  input  Reset,
  input  in_4,
  input  in_5,
  input  in_6,
  output Q,
  output out_8
);

  wire and_1_out, d_latch_1_q, d_latch_2_q, not_1_out, not_2_out, or_1_out, sr_latch_1_q, sr_latch_2_q;

  D_Latch d_latch_1 (.Q(d_latch_1_q), .D(D), .CLK(not_1_out));  // open: Q0
  D_Flip_Flop_part d_ff_1 (.D(in_4), .clk(in_5), .Q(out_8), .reset(in_6));  // open: Qn, preset
  not not_1 (not_1_out, CLK);
  SR_Latch sr_latch_1 (.Q(sr_latch_1_q), .S(Reset), .R(CLK));  // open: Q0
  and and_1 (and_1_out, CLK, sr_latch_1_q);
  not not_2 (not_2_out, or_1_out);
  SR_Latch sr_latch_2 (.Q(sr_latch_2_q), .S(Reset), .R(and_1_out));  // open: Q0
  D_Latch d_latch_2 (.Q(d_latch_2_q), .D(d_latch_1_q), .CLK(CLK));  // open: Q0
  and and_2 (Q, d_latch_2_q, not_2_out);
  or or_1 (or_1_out, sr_latch_1_q, sr_latch_2_q);
endmodule

module test (
  input  in_1,
  input  in_2,
  input  in_3,
  output out_4
);

  wire and_1_out, d_latch_1_q, d_latch_2_q, not_1_out, not_2_out, or_1_out, sr_latch_1_q;

  D_Latch d_latch_1 (.Q(d_latch_1_q), .D(in_2), .CLK(in_1));  // open: Q0
  not not_1 (not_1_out, in_1);
  SR_Latch sr_latch_1 (.Q(sr_latch_1_q), .S(in_3), .R(in_1));  // open: Q0
  and and_1 (and_1_out, d_latch_1_q, not_2_out);
  not not_2 (not_2_out, or_1_out);
  D_Latch d_latch_2 (.Q(d_latch_2_q), .D(and_1_out), .CLK(not_1_out));  // open: Q0
  and and_2 (out_4, d_latch_2_q, not_2_out);
  or or_1 (or_1_out, sr_latch_1_q, in_3);
endmodule

module test2 (
  input  in_1,
  input  in_2,
  input  in_3,
  output out_4
);

  wire and_1_out, d_latch_1_q, d_latch_2_q, not_1_out, not_2_out, or_1_out, or_2_out, sr_latch_1_q;

  not not_1 (not_1_out, in_1);
  D_Latch d_latch_1 (.Q(d_latch_1_q), .D(in_2), .CLK(not_1_out));  // open: Q0
  SR_Latch sr_latch_1 (.Q(sr_latch_1_q), .S(in_3), .R(in_1));  // open: Q0
  and and_1 (and_1_out, d_latch_1_q, not_2_out);
  or or_1 (or_1_out, in_1, or_2_out);
  D_Latch d_latch_2 (.Q(d_latch_2_q), .D(and_1_out), .CLK(or_1_out));  // open: Q0
  not not_2 (not_2_out, or_2_out);
  or or_2 (or_2_out, sr_latch_1_q, in_3);
  and and_2 (out_4, d_latch_2_q, not_2_out);
endmodule
